# Fritzing sketch Ultrasonic Radar (saved by Fritzing 0.9.4)
breadboards: 1

parts:
  Part1 = Arduino Uno (Rev3)
  U3 = HC-SR04 [chip_label=IC package="SIP (Single Inline) [THT]"]
  J1 = Basic Servo

nets:
  N1: Part1.D9_PWM, U3.Echo
  N2: Part1.D10_PWM/SS, U3.Trig
  N3: Part1.D3_PWM, J1.pulse
  VCC: Part1.5V, U3.Vcc, J1.vcc
  GND: U3.GND, J1.gnd

notes:
  HF-SRF 04]
  [Servo Motor SG90]
  [Arduino Uno R3]
  Mechatronic PRJ:
  UltraSonic Radar
  Amin Azimi
  Mehdi Heidarian

custom parts:
  HC-SR04: HC-SR04 ultrasound distance sensor
