# Fritzing sketch airQualityMonitor (saved by Fritzing 0.9.4)
breadboards: 1

parts:
  Part1 = Arduino Uno (Rev3)
  OLED_I2C1 = OLED 128x64 I2C Monochrome Display
  J1 = Piezo Speaker
  MQ-135_Breakout3 = Gas Sensor Breakout Board
  LED5 = Yellow LED - Rect 5x2x7mm [package="5x2x7 mm [THT]"]
  LED6 = Green LED - Rect 5x2x7mm [package="5x2x7 mm [THT]"]
  R2 = Resistor [tolerance=±5% resistance=220 package="2010 [SMD]"]
  LED7 = Red LED - Rect 5x2x7mm [package="5x2x7 mm [THT]"]
  R3 = Resistor [tolerance=±5% resistance=220 package="2010 [SMD]"]
  R4 = Resistor [tolerance=±5% resistance=220 package="2010 [SMD]"]

nets:
  N1: Part1.A0, MQ-135_Breakout3.GND
  N2: Part1.A4/SDA, OLED_I2C1.SCK
  N3: Part1.A5/SCL, OLED_I2C1.SDA
  N4: Part1.D8, J1.pin2
  GND: Part1.GND, OLED_I2C1.GND, J1.pin1, MQ-135_Breakout3.DOUT, R2.Pin_0, R3.Pin_0, R4.Pin_0
  N5: Part1.D3_PWM, LED6.cathode
  N6: Part1.D4, LED5.cathode
  N7: Part1.D5_PWM, LED7.cathode
  5V: Part1.5V, OLED_I2C1.VDD, MQ-135_Breakout3.5V
  N8: LED5.anode, R3.Pin_1
  N9: LED6.anode, R4.Pin_1
  N10: R2.Pin_1, LED7.anode

notes:
  [Air Quality Monitor]

custom parts:
  Gas Sensor Breakout Board: Gas sensor breakout board. Input voltage is 5V. Sensor output is available in analog and digital.
  Yellow LED - Rect 5x2x7mm: A generic rectangular yellow LED (~1.8V) 5mm x 2mm x 7mm
  Green LED - Rect 5x2x7mm: A generic rectangular green LED (~1.8V) 5mm x 2mm x 7mm
  Red LED - Rect 5x2x7mm: A generic rectangular red LED (~1.8V) 5mm x 2mm x 7mm
